# Fritzing sketch Car (saved by Fritzing 0.9.3b)

parts:
  S1 = H-Bridge with L298N
  Raspberry_Pi_Zero1 = Raspberry Pi Zero
  7_2V_NiMh = 4 x AAA Battery Mount
  U1 = SWITCH_SPDT [package=kps-1290]
  M3 = DC Motor
  M4 = DC Motor

nets:
  N1: S1.12V, U1.O
  GND: S1.GND, Raspberry_Pi_Zero1.GND, 7_2V_NiMh.+
  5V: S1.5V, Raspberry_Pi_Zero1.5V
  N2: S1.ENA, Raspberry_Pi_Zero1.GPIO21
  N3: S1.IN1, Raspberry_Pi_Zero1.GPIO5
  N4: S1.IN2, Raspberry_Pi_Zero1.GPIO6
  N5: S1.IN3, Raspberry_Pi_Zero1.GPIO19
  N6: S1.IN4, Raspberry_Pi_Zero1.GPIO26
  N7: S1.ENB, Raspberry_Pi_Zero1.GPIO20
  N8: S1.M1-01, M3.pin_1
  N9: S1.M1-02, M3.pin_2
  N10: S1.M2-01, M4.pin_1
  N11: S1.M2-02, M4.pin_2
  N12: 7_2V_NiMh.-, U1.P

custom parts:
  H-Bridge with L298N: h-bridge
